// Logisim project method2.circ as structural Verilog: 1 circuit, main circuit main
module main (
);

  wire a_rst_ones, a_rst_tens, adder_1_cout, and_1_out, and_2_out, clock_1_out;
  wire [0:0] not_1_out;
  wire [3:0] ones, ones_output, tens;

  Counter #(.max('h9), .trigger("falling"), .width(4)) counter_1 (
    .load(1'b0), .count(1'b1), .Q(tens), .up(1'b1), .clk(ones[3]), .clr(a_rst_tens));  // open: D, carry
  Counter #(.max('h9), .trigger("falling"), .width(4)) counter_2 (
    .load(1'b0), .count(1'b1), .Q(ones), .up(1'b1), .clk(clock_1_out), .clr(a_rst_ones));  // open: D, carry
  Clock clock_1 (.out(clock_1_out));
  // Probe on tens
  // Probe on ones_output
  not not_1 (not_1_out[0], tens[0]);
  Adder #(.width(4)) adder_1 (
    .a({tens[3:1], not_1_out[0]}), .b(ones), .out(ones_output), .cin(1'b0), .cout(adder_1_cout));
  // NoConnect on adder_1_cout
  and and_1 (and_1_out, ones[1], ones[0]);
  and and_2 (and_2_out, ones[3], ones[0]);
  Multiplexer multiplexer_1 (.in0(1'b0), .in1(and_1_out), .out(a_rst_tens), .sel(tens[0]));
  Multiplexer multiplexer_2 (.in0(and_2_out), .in1(and_1_out), .out(a_rst_ones), .sel(tens[0]));

  // Other names for the same wires on the sheet: tens_Qo = tens[0]

  // Notes on the sheet:
  //   hour_1
  //   hour_0
  //   Output
  //   Method 2: Adder 
  //   Adder Logic
endmodule
